# Fritzing sketch ClockMax79 (saved by Fritzing 0.9.3b)
circuit board: 16.4441cm x 11.0836cm

parts:
  Часть1 = Arduino Nano (Rev3.0)
  Сегмент2 = MAX7219 v2  # not connected
  Сегмент3 = MAX7219 v2  # not connected
  Сегмент4 = MAX7219 v2  # not connected
  ZS-042_RTC1 = ZS-042 RTC Module
  Сегмент1 = MAX7219 v2

nets:
  N1: Часть1.D10, Сегмент1.CS
  N2: Часть1.D11/MOSI, Сегмент1.CLK
  GND: Часть1.GND, ZS-042_RTC1.GND, Сегмент1.GND
  VCC: Часть1.5V, ZS-042_RTC1.VCC, Сегмент1.VCC
  N3: Часть1.A5, ZS-042_RTC1.SCL
  N4: Часть1.A4, ZS-042_RTC1.SDA
  N5: Часть1.D13/SCK, Сегмент1.DIN
