# Fritzing sketch Схема (saved by Fritzing 0.9.3b)

parts:
  Часть1 = Arduino Nano (Rev3.0)
  Grove1 = TM1637 7segment 4digit display

nets:
  N1: Часть1.D4, Grove1.DIO
  N2: Часть1.D5, Grove1.CLK
  GND: Часть1.GND, Grove1.GND
  5V: Часть1.5V, Grove1.Vcc
